// Digital circuit BoothsMultiplier.dig as structural Verilog
module BoothsMultiplier (
  input  CLK,
  input  CLR,
  input  [12:0] MULTIPLIER,
  input  [12:0] MULTIPLICAND,
  output [25:0] RESULT,
  output DONE,
  output [1:0] OP_DONE
);

  wire ACCUMULATOR_p3, and_2_out, controlunit_1_p5, F2_q, MULTIPLIER_p3, MULTIPLIER_p4, xor_1_out, xor_2_out;
  wire [12:0] ACCUMULATOR_p6, add_1_s, sub_1_s;

  xor xor_1 (xor_1_out, MULTIPLICAND[12], and_2_out);
  D_FF_AS F2 (.Set(1'b0), .D(xor_1_out), .C(ACCUMULATOR_p3), .Clr(CLR), .Q(F2_q));  // open: nQ
  Register F1 (.D(OP_DONE[0]), .C(CLK), .en(1'b1), .Q(OP_DONE[1]));
  // Shifter MULTIPLIER: pin names not known; wires that end beside it: CLK, CLR, MULTIPLIER_p3, MULTIPLIER_p4, RESULT[13], MULTIPLIER, {RESULT[12:1], OP_DONE[0]}
  // Shifter ACCUMULATOR: pin names not known; wires that end beside it: CLK, CLR, ACCUMULATOR_p3, MULTIPLIER_p4, F2_q, ACCUMULATOR_p6, RESULT[25:13]
  // ControlUnit controlunit_1: pin names not known; wires that end beside it: CLK, CLR, DONE, MULTIPLIER_p3, controlunit_1_p5, MULTIPLIER_p4
  xor xor_2 (xor_2_out, OP_DONE[1], OP_DONE[0]);
  and and_1 (ACCUMULATOR_p3, xor_2_out, controlunit_1_p5);
  and and_2 (and_2_out, ~OP_DONE[1], OP_DONE[0]);  // And
  Add #(.Bits(13)) add_1 (.a(RESULT[25:13]), .b(MULTIPLICAND), .c_i(1'b0), .s(add_1_s));  // open: c_o
  Sub #(.Bits(13)) sub_1 (.a(RESULT[25:13]), .b(MULTIPLICAND), .c_i(1'b0), .s(sub_1_s));  // open: c_o
  Multiplexer #(.Bits(13)) multiplexer_1 (.sel(and_2_out), .in_0(add_1_s), .in_1(sub_1_s), .out(ACCUMULATOR_p6));

  assign RESULT[0] = OP_DONE[0];

  // Other names for the same wires on the sheet: CLK_T = CLK

  // Notes on the sheet:
  //   CLK: Hz: 20
  //   MULTIPLIER: default 2
  //   MULTIPLICAND: default -8
  //   ShiftIn Logic
  //   IsRealOP
  //   Adder/Subtractor
endmodule
