// Digital circuit ErrorCorrection.dig as structural Verilog
module ErrorCorrection (
  input  CLK,
  input  [12:0] CODEWORD,
  input  BEGIN,
  input  CLR,
  output DONE,
  output [12:0] RESULT,
  output [3:0] EMBEDDED_VALUE,
  output ERROR_ONE,
  output ERROR_TWO,
  output [1:0] PHASE
);

  wire and_1_out, and_2_out, and_3_out, and_4_out, and_5_out, CLR_t, CODEWORD_p3, CODEWORD_p4,
       comparator_1_gt, comparator_2_eq, comparator_3_gt, comparator_3_lt, comparator_4_gt, comparator_4_lt,
       controlunit_1_p5, F1_q, multiplexer_7_out, multiplexer_11_out, not_1_out, or_1_out, or_3_out,
       or_4_out, supercontroller_1_p3, supercontroller_1_p5, xnor_1_out, xor_1_out;
  wire [12:0] add_1_s, add_2_s, counterpreset_1_out, decoder_1_out_1, multiplexer_1_out, multiplexer_2_out,
       multiplexer_3_out, multiplexer_4_out, multiplexer_5_out, multiplexer_6_out, multiplexer_8_out,
       multiplexer_9_out, multiplexer_10_out, R1, R2, R3, sub_1_s, sub_2_s;
  wire [25:0] CODEWORD_p5;

  or or_1 (or_1_out, CODEWORD_p4, CODEWORD_p3);
  // SuperController supercontroller_1: pin names not known; wires that end beside it: BEGIN, CLK, supercontroller_1_p3, PHASE, supercontroller_1_p5, DONE
  CounterPreset #(.maxValue(13), .Bits(13)) counterpreset_1 (
    .en(1'b1), .C(or_1_out), .dir(1'b0), .in(13'h1), .ld(CODEWORD_p3), .clr(1'b0), .out(counterpreset_1_out));  // open: ovf
  or or_2 (CLR_t, supercontroller_1_p5, CLR);
  Comparator #(.Bits(13)) comparator_1 (.a(counterpreset_1_out), .b(13'h7), .gt(comparator_1_gt));  // open: eq, lt
  Multiplexer #(.Selector_Bits(2), .Bits(13)) multiplexer_1 (
    .sel(PHASE), .in_0({13{1'b0}}), .in_1(CODEWORD), .in_2(CODEWORD), .in_3({{7{1'b0}}, RESULT[5:0]}),
    .out(multiplexer_1_out));
  Multiplexer #(.Selector_Bits(2), .Bits(13)) multiplexer_2 (
    .sel(PHASE), .in_0({13{1'b0}}), .in_1({13{1'b0}}), .in_2(13'h7), .in_3(13'h3), .out(multiplexer_2_out));
  Comparator #(.Bits(2)) comparator_2 (.a(PHASE), .b(2'b11), .eq(comparator_2_eq));  // open: gt, lt
  or or_3 (or_3_out, CODEWORD_p3, and_3_out);
  D_FF #(.Bits(13)) d_ff_1 (.D(multiplexer_3_out), .C(or_4_out), .Q(R3));  // open: nQ
  Multiplexer #(.Bits(13)) multiplexer_3 (.sel(BEGIN), .in_0(R2), .in_1({13{1'b0}}), .out(multiplexer_3_out));
  and and_1 (and_1_out, comparator_1_gt, comparator_2_eq);
  D_FF #(.Bits(13)) d_ff_2 (.D(multiplexer_5_out), .C(or_4_out), .Q(R2));  // open: nQ
  and and_2 (and_2_out, or_3_out, ~and_1_out);  // And
  Multiplexer #(.Bits(13)) multiplexer_4 (
    .sel(CODEWORD_p3), .in_0(multiplexer_10_out), .in_1(multiplexer_2_out), .out(multiplexer_4_out));
  Multiplexer #(.Bits(13)) multiplexer_5 (
    .sel(BEGIN), .in_0({R1[12:5], EMBEDDED_VALUE, R1[0]}), .in_1({13{1'b0}}), .out(multiplexer_5_out));
  Register F1 (.D(CODEWORD_p5[0]), .C(CLK), .en(1'b1), .Q(F1_q));
  // Shifter CODEWORD: pin names not known; wires that end beside it: CLK, CLR_t, CODEWORD_p3, CODEWORD_p4, CODEWORD_p5[13], multiplexer_1_out, CODEWORD_p5[12:0]
  // Shifter ACCUMULATOR: pin names not known; wires that end beside it: CLK, CLR_t, and_2_out, 1'b0, 1'b0, multiplexer_4_out, CODEWORD_p5[25:13]
  // ControlUnit controlunit_1: pin names not known; wires that end beside it: CLK, supercontroller_1_p5, supercontroller_1_p3, CODEWORD_p3, controlunit_1_p5, CODEWORD_p4
  D_FF #(.Bits(13)) d_ff_3 (.D(multiplexer_6_out), .C(or_4_out), .Q({R1[12:5], EMBEDDED_VALUE, R1[0]}));  // open: nQ
  or or_4 (or_4_out, supercontroller_1_p3, BEGIN);
  Multiplexer #(.Bits(13)) multiplexer_6 (
    .sel(BEGIN), .in_0(CODEWORD_p5[25:13]), .in_1({13{1'b0}}), .out(multiplexer_6_out));
  and and_3 (and_3_out, multiplexer_7_out, controlunit_1_p5);
  xor xor_1 (xor_1_out, F1_q, CODEWORD_p5[0]);
  Multiplexer #(.Selector_Bits(2)) multiplexer_7 (
    .sel(PHASE), .in_0(1'b0), .in_1(xor_1_out), .in_2(xnor_1_out), .in_3(xnor_1_out), .out(multiplexer_7_out));
  Multiplexer #(.Selector_Bits(2), .Bits(13)) multiplexer_8 (
    .sel(PHASE), .in_0(R2), .in_1({R1[12:5], EMBEDDED_VALUE, R1[0]}), .in_2(CODEWORD_p5[25:13]),
    .in_3({R1[12:5], EMBEDDED_VALUE, R1[0]}), .out(multiplexer_8_out));
  and and_4 (and_4_out, ~F1_q, CODEWORD_p5[0]);  // And
  xnor xnor_1 (xnor_1_out, F1_q, CODEWORD_p5[0]);
  Add #(.Bits(13)) add_1 (.a(CODEWORD_p5[25:13]), .b(counterpreset_1_out), .c_i(1'b0), .s(add_1_s));  // open: c_o
  Sub #(.Bits(13)) sub_1 (.a(CODEWORD_p5[25:13]), .b(counterpreset_1_out), .c_i(1'b0), .s(sub_1_s));  // open: c_o
  and and_5 (and_5_out, F1_q, CODEWORD_p5[0]);
  Add #(.Bits(13)) add_2 (.a({13{1'b0}}), .b(multiplexer_8_out), .c_i(1'b0), .s(add_2_s));  // open: c_o
  Sub #(.Bits(13)) sub_2 (.a({13{1'b0}}), .b(multiplexer_8_out), .c_i(1'b0), .s(sub_2_s));  // open: c_o
  not not_1 (not_1_out, and_5_out);
  Multiplexer #(.Bits(13)) multiplexer_9 (
    .sel(multiplexer_8_out[12]), .in_0(add_2_s), .in_1(sub_2_s), .out(multiplexer_9_out));
  Multiplexer #(.Bits(13)) multiplexer_10 (
    .sel(multiplexer_11_out), .in_0(add_1_s), .in_1(sub_1_s), .out(multiplexer_10_out));
  Multiplexer #(.Selector_Bits(2)) multiplexer_11 (
    .sel(PHASE), .in_0(1'b0), .in_1(and_4_out), .in_2(not_1_out), .in_3(not_1_out), .out(multiplexer_11_out));
  Comparator #(.Bits(13)) comparator_3 (.a(R3), .b(13'h6), .gt(comparator_3_gt), .lt(comparator_3_lt));  // open: eq
  or or_5 (ERROR_ONE, comparator_3_gt, comparator_3_lt);
  Decoder #(.Selector_Bits(4)) decoder_1 (
    .sel(multiplexer_9_out[4:1]), .out_1(decoder_1_out_1[0]), .out_2(decoder_1_out_1[1]),
    .out_3(decoder_1_out_1[2]), .out_4(decoder_1_out_1[3]), .out_5(decoder_1_out_1[4]),
    .out_6(decoder_1_out_1[5]), .out_7(decoder_1_out_1[6]), .out_8(decoder_1_out_1[7]),
    .out_9(decoder_1_out_1[8]), .out_10(decoder_1_out_1[9]), .out_11(decoder_1_out_1[10]),
    .out_12(decoder_1_out_1[11]), .out_13(decoder_1_out_1[12]));  // open: out_0, out_14, out_15
  assign RESULT = CODEWORD ^ decoder_1_out_1;  // XOr xor_2, 13 bits wide
  Comparator #(.Bits(13)) comparator_4 (
    .a(R2), .b({13{1'b0}}), .gt(comparator_4_gt), .lt(comparator_4_lt));  // open: eq
  or or_6 (ERROR_TWO, comparator_4_gt, comparator_4_lt);

  // Other names for the same wires on the sheet: CLK_T = CLK; CODE[12:0] = CODEWORD; COR[12:0] = RESULT;
  //   R1[4:1] = EMBEDDED_VALUE

  // Notes on the sheet:
  //   CLK: Hz: 609
  //   CODEWORD: default 504
  //   IsRealOP
  //   Adder/Subtractor
endmodule
